// Logisim project basicgates.circ as structural Verilog: 16 circuits, main circuit main
module main (
);

  wire adder64bit_1_overflow, subtractor1bit_1_borrow, subtractor1bit_1_output1;
  wire [63:0] adder64bit_1_output1, negate64bit_1_output1;

  // Probe on adder64bit_1_overflow
  adder64bit adder64bit_1 (
    .inflow(1'b1), .input1({64{1'b1}}), .input2({64{1'b1}}), .overflow(adder64bit_1_overflow),
    .output1(adder64bit_1_output1));
  // Probe on adder64bit_1_output1
  // Probe on negate64bit_1_output1
  negate64bit negate64bit_1 (.input1({64{1'b1}}), .output1(negate64bit_1_output1));
  // Probe on subtractor1bit_1_borrow
  subtractor1bit subtractor1bit_1 (
    .inborrow(1'b0), .input1(1'b0), .input2(1'b0), .borrow(subtractor1bit_1_borrow),
    .output1(subtractor1bit_1_output1));
  // Probe on subtractor1bit_1_output1
endmodule

module adder1bit (
  input  inflow,
  input  input1,
  input  input2,
  output overflow,
  output output1
);

  wire and_1_out, and_2_out, xor_1_out;

  and and_1 (and_1_out, input1, input2);
  xor xor_1 (xor_1_out, input1, input2);
  and and_2 (and_2_out, inflow, xor_1_out);
  xor xor_2 (output1, inflow, xor_1_out);
  or or_1 (overflow, and_1_out, and_2_out);
endmodule

module adder2bit (
  input  inflow,
  input  [1:0] input1,
  input  [1:0] input2,
  output overflow,
  output [1:0] output1
);

  wire adder1bit_1_overflow;

  adder1bit adder1bit_1 (
    .inflow(inflow), .input1(input1[0]), .input2(input2[0]), .overflow(adder1bit_1_overflow),
    .output1(output1[0]));
  adder1bit adder1bit_2 (
    .inflow(adder1bit_1_overflow), .input1(input1[1]), .input2(input2[1]), .overflow(overflow),
    .output1(output1[1]));
endmodule

module adder4bit (
  input  inflow,
  input  [3:0] input1,
  input  [3:0] input2,
  output overflow,
  output [3:0] output1
);

  wire adder2bit_1_overflow;

  adder2bit adder2bit_1 (
    .inflow(inflow), .input1(input1[1:0]), .input2(input2[1:0]), .overflow(adder2bit_1_overflow),
    .output1(output1[1:0]));
  adder2bit adder2bit_2 (
    .inflow(adder2bit_1_overflow), .input1(input1[3:2]), .input2(input2[3:2]), .overflow(overflow),
    .output1(output1[3:2]));
endmodule

module adder8bit (
  input  inflow,
  input  [7:0] input1,
  input  [7:0] input2,
  output overflow,
  output [7:0] output1
);

  wire adder4bit_1_overflow;

  adder4bit adder4bit_1 (
    .inflow(inflow), .input1(input1[3:0]), .input2(input2[3:0]), .overflow(adder4bit_1_overflow),
    .output1(output1[3:0]));
  adder4bit adder4bit_2 (
    .inflow(adder4bit_1_overflow), .input1(input1[7:4]), .input2(input2[7:4]), .overflow(overflow),
    .output1(output1[7:4]));
endmodule

module adder16bit (
  input  inflow,
  input  [15:0] input1,
  input  [15:0] input2,
  output overflow,
  output [15:0] output1
);

  wire adder8bit_1_overflow;

  adder8bit adder8bit_1 (
    .inflow(inflow), .input1(input1[7:0]), .input2(input2[7:0]), .overflow(adder8bit_1_overflow),
    .output1(output1[7:0]));
  adder8bit adder8bit_2 (
    .inflow(adder8bit_1_overflow), .input1(input1[15:8]), .input2(input2[15:8]), .overflow(overflow),
    .output1(output1[15:8]));
endmodule

module adder32bit (
  input  inflow,
  input  [31:0] input1,
  input  [31:0] input2,
  output overflow,
  output [31:0] output1
);

  wire adder16bit_1_overflow;

  adder16bit adder16bit_1 (
    .inflow(inflow), .input1(input1[15:0]), .input2(input2[15:0]), .overflow(adder16bit_1_overflow),
    .output1(output1[15:0]));
  adder16bit adder16bit_2 (
    .inflow(adder16bit_1_overflow), .input1(input1[31:16]), .input2(input2[31:16]), .overflow(overflow),
    .output1(output1[31:16]));
endmodule

module adder64bit (
  input  inflow,
  input  [63:0] input1,
  input  [63:0] input2,
  output overflow,
  output [63:0] output1
);

  wire adder32bit_1_overflow;

  adder32bit adder32bit_1 (
    .inflow(inflow), .input1(input1[31:0]), .input2(input2[31:0]), .overflow(adder32bit_1_overflow),
    .output1(output1[31:0]));
  adder32bit adder32bit_2 (
    .inflow(adder32bit_1_overflow), .input1(input1[63:32]), .input2(input2[63:32]), .overflow(overflow),
    .output1(output1[63:32]));
endmodule

module negate1bit (
  input  input1,
  output output1
);


  assign output1 = input1;
endmodule

module negate2bit (
  input  [1:0] input1,
  output [1:0] output1
);

  wire [1:0] not_1_out;

  assign not_1_out = ~input1;  // NOT_Gate not_1, 2 bits wide
  adder2bit adder2bit_1 (.input1(2'b01), .input2(not_1_out), .output1(output1));  // open: inflow, overflow
endmodule

module negate4bit (
  input  [3:0] input1,
  output [3:0] output1
);

  wire [3:0] not_1_out;

  assign not_1_out = ~input1;  // NOT_Gate not_1, 4 bits wide
  adder4bit adder4bit_1 (.input1(4'b0001), .input2(not_1_out), .output1(output1));  // open: inflow, overflow
endmodule

module negate8bit (
  input  [7:0] input1,
  output [7:0] output1
);

  wire [7:0] not_1_out;

  assign not_1_out = ~input1;  // NOT_Gate not_1, 8 bits wide
  adder8bit adder8bit_1 (.input1(8'h1), .input2(not_1_out), .output1(output1));  // open: inflow, overflow
endmodule

module negate16bit (
  input  [15:0] input1,
  output [15:0] output1
);

  wire [15:0] not_1_out;

  assign not_1_out = ~input1;  // NOT_Gate not_1, 16 bits wide
  adder16bit adder16bit_1 (.input1(16'h1), .input2(not_1_out), .output1(output1));  // open: inflow, overflow
endmodule

module negate32bit (
  input  [31:0] input1,
  output [31:0] output1
);

  wire [31:0] not_1_out;

  assign not_1_out = ~input1;  // NOT_Gate not_1, 32 bits wide
  adder32bit adder32bit_1 (.input1(32'h1), .input2(not_1_out), .output1(output1));  // open: inflow, overflow
endmodule

module negate64bit (
  input  [63:0] input1,
  output [63:0] output1
);

  wire [63:0] not_1_out;

  assign not_1_out = ~input1;  // NOT_Gate not_1, 64 bits wide
  adder64bit adder64bit_1 (.input1(64'h1), .input2(not_1_out), .output1(output1));  // open: inflow, overflow
endmodule

module subtractor1bit (
  input  inborrow,
  input  input1,
  input  input2,
  output borrow,
  output output1
);

  wire and_1_out, and_2_out, not_1_out, not_2_out, subtractor_1_bout, subtractor_1_out, xor_1_out;

  // Probe on subtractor_1_out
  Subtractor #(.width(1)) subtractor_1 (
    .a(1'b0), .b(1'b0), .out(subtractor_1_out), .bin(1'b0), .bout(subtractor_1_bout));
  // Probe on subtractor_1_bout
  not not_1 (not_1_out, input1);
  xor xor_1 (xor_1_out, input1, input2);
  and and_1 (and_1_out, not_1_out, input2);
  and and_2 (and_2_out, inborrow, not_2_out);
  not not_2 (not_2_out, xor_1_out);
  xor xor_2 (output1, inborrow, xor_1_out);
  or or_1 (borrow, and_1_out, and_2_out);
endmodule
