// Logisim project muxrisccore.circ as structural Verilog: 3 circuits, main circuit core
module core (
);

  wire alu_1_we, and_1_out, and_2_out, and_3_out, and_4_out, and_5_out, and_6_out, bitselector_8_out,
       bitselector_9_out, clock_1_out, clock_2_out, clock_3_out, clock_4_out, clock_5_out, clock_6_out,
       clock_7_out, clock_8_out, comparator_1_eq, comparator_2_eq, comparator_3_eq, comparator_4_eq,
       comparator_5_eq, comparator_5_gt, comparator_5_lt, comparator_6_eq, comparator_7_eq, comparator_7_gt,
       comparator_7_lt, multiplexer_1_out, not_1_out, not_2_out, not_3_out, not_4_out, not_5_out, or_1_out,
       regX_p2;
  wire [1:0] bitselector_10_out;
  wire [3:0] bitselector_6_out, bitselector_7_out;
  wire [7:0] bitselector_5_out;
  wire [8:0] bitselector_14_out, bitselector_18_out;
  wire [15:0] bitselector_1_out, bitselector_2_out, bitselector_3_out, bitselector_4_out, bitselector_11_out,
       bitselector_12_out;
  wire [23:0] bitselector_13_out, bitselector_16_out, bitselector_17_out, ram1_p1, ram1_p2;
  wire [31:0] counter_1_q;
  wire [63:0] alu_1_outx, alu_2_outx, alu_3_outx, alu_4_outx, alu_5_outx, alu_6_outx, alu_7_outx, alu_8_outx,
       multiplexer_10_out, multiplexer_11_out, multiplexer_12_out, multiplexer_13_out, multiplexer_14_out,
       multiplexer_15_out, multiplexer_16_out, multiplexer_17_out, ram1_p3, regX_p12, regX_p13, regX_p14,
       regX_p15, regX_p16, regX_p17, regX_p18, regX_p19, regX_p20, regX_p21, regX_p22, regX_p23, regX_p24,
       regX_p25, regX_p26, regX_p27, regY_p10, regY_p11, regY_p12, regY_p13, regY_p14, regY_p15, regY_p16,
       regY_p17, regZ_p10, regZ_p11, regZ_p12, regZ_p13, regZ_p14, regZ_p15, regZ_p16, regZ_p17, rom1_p38,
       rom1_p39, rom1_p40, rom1_p41, rom1_p42, rom1_p43, rom1_p44, rom1_p45, rom1_p46, rom1_p47, rom1_p48,
       rom1_p49, rom1_p50, rom1_p51, rom1_p52, rom1_p53;

  BitSelector #(.group(16), .width(64)) bitselector_1 (.in(ram1_p3), .out(bitselector_1_out), .sel(2'b11));
  BitSelector #(.group(16), .width(64)) bitselector_2 (.in(ram1_p3), .out(bitselector_2_out), .sel(2'b10));
  BitSelector #(.group(16), .width(64)) bitselector_3 (.in(ram1_p3), .out(bitselector_3_out), .sel(2'b01));
  BitSelector #(.group(16), .width(64)) bitselector_4 (.in(ram1_p3), .out(bitselector_4_out), .sel(2'b00));
  BitSelector #(.group(8), .width(16)) bitselector_5 (.in(bitselector_4_out), .out(bitselector_5_out), .sel(1'b1));
  BitSelector #(.group(4), .width(16)) bitselector_6 (.in(bitselector_4_out), .out(bitselector_6_out), .sel(2'b01));
  BitSelector #(.group(4), .width(16)) bitselector_7 (.in(bitselector_4_out), .out(bitselector_7_out), .sel(2'b00));
  Clock clock_1 (.out(clock_1_out));
  BitSelector #(.width(4)) bitselector_8 (.in(bitselector_6_out), .out(bitselector_8_out), .sel(2'b00));
  // RAM #(.addrWidth(16), .dataWidth(64), .enables("line"), .line("octo"), .misaligned("true")) regX: pin names not known; wires that end beside it: bitselector_1_out, regX_p2, regX_p2, bitselector_5_out[1], bitselector_5_out[2], bitselector_5_out[3], bitselector_5_out[4], bitselector_5_out[5], bitselector_5_out[6], bitselector_5_out[7], clock_1_out, regX_p12, regX_p13, regX_p14, regX_p15, regX_p16, regX_p17, regX_p18, regX_p19, regX_p20, regX_p21, regX_p22, regX_p23, regX_p24, regX_p25, regX_p26, regX_p27
  Comparator #(.mode("unsigned"), .width(4)) comparator_1 (
    .a(bitselector_7_out), .b(4'b0000), .eq(comparator_1_eq));  // open: gt, lt
  Counter #(.max('hffffffff), .width(32)) counter_1 (
    .load(or_1_out), .D({32{1'b0}}), .count(comparator_1_eq), .Q(counter_1_q), .clk(clock_2_out));  // open: carry, up, clr
  Clock clock_2 (.out(clock_2_out));
  Comparator #(.mode("unsigned"), .width(4)) comparator_2 (
    .a(bitselector_7_out), .b(4'b0001), .eq(comparator_2_eq));  // open: gt, lt
  not not_1 (not_1_out, bitselector_8_out);
  Comparator #(.mode("unsigned"), .width(4)) comparator_3 (
    .a(bitselector_7_out), .b(4'b0010), .eq(comparator_3_eq));  // open: gt, lt
  Comparator #(.mode("unsigned"), .width(4)) comparator_4 (
    .a(bitselector_7_out), .b(4'b0011), .eq(comparator_4_eq));  // open: gt, lt
  BitSelector #(.width(4)) bitselector_9 (.in(bitselector_6_out), .out(bitselector_9_out), .sel(2'b00));
  Comparator #(.mode("unsigned"), .width(32)) comparator_5 (
    .a(counter_1_q), .b({bitselector_2_out, bitselector_3_out}), .gt(comparator_5_gt), .eq(comparator_5_eq),
    .lt(comparator_5_lt));
  Comparator #(.mode("unsigned"), .width(64)) comparator_6 (
    .a(regY_p10), .b({64{1'b0}}), .eq(comparator_6_eq));  // open: gt, lt
  not not_2 (not_2_out, bitselector_9_out);
  or or_1 (or_1_out, comparator_5_gt, comparator_5_eq);
  and and_1 (and_1_out, comparator_5_lt, comparator_1_eq);
  not not_3 (not_3_out, comparator_6_eq);
  and and_2 (and_2_out, not_3_out, comparator_2_eq);
  and and_3 (and_3_out, comparator_4_eq, not_2_out);
  and and_4 (and_4_out, comparator_4_eq, bitselector_9_out);
  or or_2 (regX_p2, comparator_3_eq, and_3_out, alu_1_we);
  Multiplexer multiplexer_1 (.in0(and_2_out), .in1(comparator_2_eq), .out(multiplexer_1_out), .sel(not_1_out));
  alu alu_1 (
    .argX(regX_p20), .argY(regY_p10), .argZ(regZ_p10), .op(bitselector_7_out), .\var (bitselector_6_out),
    .outX(alu_1_outx), .we(alu_1_we));
  Multiplexer #(.select(4), .width(64)) multiplexer_2 (
    .in2({{32{1'b0}}, bitselector_2_out, bitselector_3_out}), .in3(multiplexer_10_out), .in4(alu_1_outx),
    .in5(alu_1_outx), .in6(alu_1_outx), .in7(alu_1_outx), .in8(alu_1_outx), .out(regX_p12),
    .sel(bitselector_7_out));  // open: in0, in1, in9, in10, in11, in12, in13, in14, in15
  alu alu_2 (
    .argX(regX_p21), .argY(regY_p11), .argZ(regZ_p11), .op(bitselector_7_out), .\var (bitselector_6_out),
    .outX(alu_2_outx));  // open: we
  Multiplexer #(.select(4), .width(64)) multiplexer_3 (
    .in2({{32{1'b0}}, bitselector_2_out, bitselector_3_out}), .in3(multiplexer_11_out), .in4(alu_2_outx),
    .in5(alu_2_outx), .in6(alu_2_outx), .in7(alu_2_outx), .in8(alu_2_outx), .out(regX_p13),
    .sel(bitselector_7_out));  // open: in0, in1, in9, in10, in11, in12, in13, in14, in15
  // DualRAM #(.addrWidth(16), .dataWidth(64), .enables("line"), .line("octo"), .misaligned("true"), .\type ("nonvolatile")) regY: pin names not known; wires that end beside it: bitselector_2_out, bitselector_1_out, regX_p2, regX_p2, bitselector_5_out[1], bitselector_5_out[2], bitselector_5_out[3], bitselector_5_out[4], bitselector_5_out[5], regY_p10, regY_p11, regY_p12, regY_p13, regY_p14, regY_p15, regY_p16, regY_p17
  Clock clock_3 (.out(clock_3_out));
  alu alu_3 (
    .argX(regX_p22), .argY(regY_p12), .argZ(regZ_p12), .op(bitselector_7_out), .\var (bitselector_6_out),
    .outX(alu_3_outx));  // open: we
  Multiplexer #(.select(4), .width(64)) multiplexer_4 (
    .in2({{32{1'b0}}, bitselector_2_out, bitselector_3_out}), .in3(multiplexer_12_out), .in4(alu_3_outx),
    .in5(alu_3_outx), .in6(alu_3_outx), .in7(alu_3_outx), .in8(alu_3_outx), .out(regX_p14),
    .sel(bitselector_7_out));  // open: in0, in1, in9, in10, in11, in12, in13, in14, in15
  alu alu_4 (
    .argX(regX_p23), .argY(regY_p13), .argZ(regZ_p13), .op(bitselector_7_out), .\var (bitselector_6_out),
    .outX(alu_4_outx));  // open: we
  Multiplexer #(.select(4), .width(64)) multiplexer_5 (
    .in2({{32{1'b0}}, bitselector_2_out, bitselector_3_out}), .in3(multiplexer_13_out), .in4(alu_4_outx),
    .in5(alu_4_outx), .in6(alu_4_outx), .in7(alu_4_outx), .in8(alu_4_outx), .out(regX_p15),
    .sel(bitselector_7_out));  // open: in0, in1, in9, in10, in11, in12, in13, in14, in15
  alu alu_5 (
    .argX(regX_p24), .argY(regY_p14), .argZ(regZ_p14), .op(bitselector_7_out), .\var (bitselector_6_out),
    .outX(alu_5_outx));  // open: we
  Multiplexer #(.select(4), .width(64)) multiplexer_6 (
    .in2({{32{1'b0}}, bitselector_2_out, bitselector_3_out}), .in3(multiplexer_14_out), .in4(alu_5_outx),
    .in5(alu_5_outx), .in6(alu_5_outx), .in7(alu_5_outx), .in8(alu_5_outx), .out(regX_p16),
    .sel(bitselector_7_out));  // open: in0, in1, in9, in10, in11, in12, in13, in14, in15
  alu alu_6 (
    .argX(regX_p25), .argY(regY_p15), .argZ(regZ_p15), .op(bitselector_7_out), .\var (bitselector_6_out),
    .outX(alu_6_outx));  // open: we
  Multiplexer #(.select(4), .width(64)) multiplexer_7 (
    .in2({{32{1'b0}}, bitselector_2_out, bitselector_3_out}), .in3(multiplexer_15_out), .in4(alu_6_outx),
    .in5(alu_6_outx), .in6(alu_6_outx), .in7(alu_6_outx), .in8(alu_6_outx), .out(regX_p17),
    .sel(bitselector_7_out));  // open: in0, in1, in9, in10, in11, in12, in13, in14, in15
  alu alu_7 (
    .argX(regX_p26), .argY(regY_p16), .argZ(regZ_p16), .op(bitselector_7_out), .\var (bitselector_6_out),
    .outX(alu_7_outx));  // open: we
  Multiplexer #(.select(4), .width(64)) multiplexer_8 (
    .in2({{32{1'b0}}, bitselector_2_out, bitselector_3_out}), .in3(multiplexer_16_out), .in4(alu_7_outx),
    .in5(alu_7_outx), .in6(alu_7_outx), .in7(alu_7_outx), .in8(alu_7_outx), .out(regX_p18),
    .sel(bitselector_7_out));  // open: in0, in1, in9, in10, in11, in12, in13, in14, in15
  alu alu_8 (
    .argX(regX_p27), .argY(regY_p17), .argZ(regZ_p17), .op(bitselector_7_out), .\var (bitselector_6_out),
    .outX(alu_8_outx));  // open: we
  Multiplexer #(.select(4), .width(64)) multiplexer_9 (
    .in2({{32{1'b0}}, bitselector_2_out, bitselector_3_out}), .in3(multiplexer_17_out), .in4(alu_8_outx),
    .in5(alu_8_outx), .in6(alu_8_outx), .in7(alu_8_outx), .in8(alu_8_outx), .out(regX_p19),
    .sel(bitselector_7_out));  // open: in0, in1, in9, in10, in11, in12, in13, in14, in15
  BitSelector #(.group(2), .width(64)) bitselector_10 (.in(regY_p10), .out(bitselector_10_out), .sel({5{1'b1}}));
  Clock clock_4 (.out(clock_4_out));
  Comparator #(.mode("unsigned"), .width(2)) comparator_7 (
    .a(bitselector_10_out), .b(2'b01), .gt(comparator_7_gt), .eq(comparator_7_eq), .lt(comparator_7_lt));
  // DualRAM #(.addrWidth(16), .dataWidth(64), .enables("line"), .line("octo"), .misaligned("true"), .\type ("nonvolatile")) regZ: pin names not known; wires that end beside it: bitselector_3_out, bitselector_1_out, regX_p2, regX_p2, bitselector_5_out[1], bitselector_5_out[2], bitselector_5_out[3], bitselector_5_out[4], bitselector_5_out[5], regZ_p10, regZ_p11, regZ_p12, regZ_p13, regZ_p14, regZ_p15, regZ_p16, regZ_p17
  not not_4 (not_4_out, comparator_7_lt);
  BitSelector #(.group(16), .width(64)) bitselector_11 (.in(regY_p10), .out(bitselector_11_out), .sel(2'b00));
  BitSelector #(.group(16), .width(64)) bitselector_12 (.in(regY_p10), .out(bitselector_12_out), .sel(2'b01));
  not not_5 (not_5_out, and_1_out);
  BitSelector #(.group(24), .width(64)) bitselector_13 (.in(regX_p20), .out(bitselector_13_out), .sel(2'b00));
  and and_5 (and_5_out, comparator_7_lt, and_4_out);
  Clock clock_5 (.out(clock_5_out));
  and and_6 (and_6_out, comparator_7_eq, and_4_out);
  Clock clock_6 (.out(clock_6_out));
  BitSelector #(.group(9), .width(16)) bitselector_14 (.in(bitselector_12_out), .out(bitselector_14_out), .sel(1'b0));
  Clock clock_7 (.out(clock_7_out));
  // DualRAM #(.addrWidth(24), .dataWidth(64), .enables("line"), .line("octo"), .misaligned("true"), .\type ("nonvolatile")) ram1: pin names not known; wires that end beside it: ram1_p1, ram1_p2, ram1_p3
  Counter #(.max('hffffff), .trigger("falling"), .width(24)) counter_2 (
    .load(multiplexer_1_out), .D(bitselector_13_out), .count(not_5_out), .Q(ram1_p1), .clk(clock_8_out));  // open: carry, up, clr
  Clock clock_8 (.out(clock_8_out));
  BitSelector #(.group(24), .width(64)) bitselector_15 (.in(regY_p10), .out(ram1_p2), .sel(2'b00));
  BitSelector #(.group(24), .width(64)) bitselector_16 (.in(regY_p10), .out(bitselector_16_out), .sel(2'b00));
  // RAM #(.addrWidth(24), .dataWidth(64), .enables("line"), .line("octo"), .misaligned("true")) rom1: pin names not known; wires that end beside it: and_5_out, and_5_out, bitselector_5_out[1], bitselector_5_out[2], bitselector_5_out[3], bitselector_5_out[4], bitselector_5_out[5], bitselector_5_out[6], bitselector_5_out[7], clock_5_out, regX_p20, regX_p21, regX_p22, regX_p23, regX_p24, regX_p25, regX_p26, regX_p27, bitselector_16_out, and_6_out, and_6_out, bitselector_5_out[1], bitselector_5_out[2], bitselector_5_out[3], bitselector_5_out[4], bitselector_5_out[5], bitselector_5_out[6], bitselector_5_out[7], clock_6_out, regX_p20, regX_p21, regX_p22, regX_p23, regX_p24, regX_p25, regX_p26, regX_p27, rom1_p38, rom1_p39, rom1_p40, rom1_p41, rom1_p42, rom1_p43, rom1_p44, rom1_p45, rom1_p46, rom1_p47, rom1_p48, rom1_p49, rom1_p50, rom1_p51, rom1_p52, rom1_p53
  BitSelector #(.group(24), .width(64)) bitselector_17 (.in(regX_p20), .out(bitselector_17_out), .sel(2'b00));
  BitSelector #(.group(9), .width(16)) bitselector_18 (.in(bitselector_11_out), .out(bitselector_18_out), .sel(1'b0));
  // RGB_Video #(.cursor("No Cursor"), .height(512), .scale(1), .width(512)) rgb_video_1: pin names not known; wires that end beside it: clock_7_out, comparator_7_gt, bitselector_14_out, bitselector_18_out, bitselector_17_out
  Multiplexer #(.width(64)) multiplexer_10 (.in0(rom1_p38), .in1(rom1_p46), .out(multiplexer_10_out), .sel(not_4_out));
  Multiplexer #(.width(64)) multiplexer_11 (.in0(rom1_p39), .in1(rom1_p47), .out(multiplexer_11_out), .sel(not_4_out));
  Multiplexer #(.width(64)) multiplexer_12 (.in0(rom1_p40), .in1(rom1_p48), .out(multiplexer_12_out), .sel(not_4_out));
  Multiplexer #(.width(64)) multiplexer_13 (.in0(rom1_p41), .in1(rom1_p49), .out(multiplexer_13_out), .sel(not_4_out));
  Multiplexer #(.width(64)) multiplexer_14 (.in0(rom1_p42), .in1(rom1_p50), .out(multiplexer_14_out), .sel(not_4_out));
  Multiplexer #(.width(64)) multiplexer_15 (.in0(rom1_p43), .in1(rom1_p51), .out(multiplexer_15_out), .sel(not_4_out));
  Multiplexer #(.width(64)) multiplexer_16 (.in0(rom1_p44), .in1(rom1_p52), .out(multiplexer_16_out), .sel(not_4_out));
  Multiplexer #(.width(64)) multiplexer_17 (.in0(rom1_p45), .in1(rom1_p53), .out(multiplexer_17_out), .sel(not_4_out));
endmodule

module alu (
  input  [63:0] argX,
  input  [63:0] argY,
  input  [63:0] argZ,
  input  [3:0] op,
  input  [3:0] \var ,
  output [63:0] outX,
  output we
);

  wire adder_1_cout, and_2_out, and_3_out, and_4_out, and_5_out, bitfinder_1_found, bitfinder_2_found,
       bitfinder_3_found, bitfinder_4_found, bitselector_3_out, clock_1_out, clock_2_out, clock_3_out,
       comparator_1_eq, comparator_2_eq, comparator_2_lt, comparator_3_eq, comparator_4_eq, comparator_5_eq,
       comparator_6_eq, comparator_7_eq, comparator_8_eq, comparator_9_eq, comparator_10_eq,
       comparator_11_eq, comparator_12_eq, comparator_13_eq, fpclassificator_1_p1, fpclassificator_1_p2,
       fpcomparator_1_p6, fpcomparator_1_p7, multiplexer_1_out, not_2_out, not_3_out, not_4_out,
       subtractor_1_bout;
  wire [1:0] bitselector_2_out;
  wire [5:0] bitfinder_1_index, bitfinder_2_index, bitfinder_3_index, bitfinder_4_index, bitselector_1_out;
  wire [6:0] bitadder_1_out;
  wire [63:0] adder_1_out, and_1_out, bit_extender_1_out, bit_extender_2_out, bit_extender_3_out,
       bit_extender_4_out, bit_extender_5_out, bit_extender_6_out, bit_extender_7_out, bit_extender_8_out,
       bit_extender_9_out, buffer_1_out, buffer_2_out, counter_1_q, divider_1_out, divider_1_rem,
       fpadder_1_out, fpdivider_1_out, fpexponentiator_1_p1, fplogarithm_1_p3, fpmultiplier_1_out,
       fpnegator_1_p2, fpsquareroot_1_p1, fpsubtractor_1_out, fptoint_1_p1, fptoint_2_p1, fptoint_3_p1,
       fptoint_4_p1, fptrigonometry_1_p4, fptrigonometry_1_p5, fptrigonometry_1_p6, fptrigonometry_2_p2,
       fptrigonometry_2_p3, fptrigonometry_2_p4, inttofp_1_p1, multiplexer_2_out, multiplexer_3_out,
       multiplexer_4_out, multiplexer_5_out, multiplexer_6_out, multiplexer_7_out, multiplexer_8_out,
       multiplexer_9_out, multiplexer_10_out, multiplexer_11_out, multiplexer_12_out, multiplexer_13_out,
       multiplexer_14_out, multiplier_1_cout, multiplier_1_out, nand_1_out, negator_1_out, nor_1_out,
       not_1_out, or_1_out, register_1_q, shifter_1_out, shifter_2_out, shifter_3_out, shifter_4_out,
       shifter_5_out, subtractor_1_out, undriven, xnor_1_out, xor_1_out;

  BitSelector #(.group(6), .width(64)) bitselector_1 (.in(argZ), .out(bitselector_1_out), .sel(4'b0000));
  Comparator #(.mode("unsigned"), .width(4)) comparator_1 (.a(op), .b(4'b0100), .eq(comparator_1_eq));  // open: gt, lt
  BitSelector #(.group(2), .width(4)) bitselector_2 (.in(\var ), .out(bitselector_2_out), .sel(1'b0));
  Comparator #(.width(64)) comparator_2 (
    .a(argY), .b({64{1'b0}}), .eq(comparator_2_eq), .lt(comparator_2_lt));  // open: gt
  // FPComparator #(.fpwidth(64)) fpcomparator_1: pin names not known; wires that end beside it: argX, argY, argZ, argY, {64{1'b0}}, fpcomparator_1_p6, fpcomparator_1_p7
  Comparator #(.mode("unsigned"), .width(4)) comparator_3 (.a(op), .b(4'b0101), .eq(comparator_3_eq));  // open: gt, lt
  Adder #(.width(64)) adder_1 (.a(argZ), .b(argY), .out(adder_1_out), .cout(adder_1_cout));  // open: cin
  assign bit_extender_1_out = {{63{1'b0}}, adder_1_cout};  // Bit_Extender bit_extender_1
  Comparator #(.mode("unsigned"), .width(4)) comparator_4 (.a(op), .b(4'b0110), .eq(comparator_4_eq));  // open: gt, lt
  Shifter #(.width(64)) shifter_1 (.in(argY), .\dist (bitselector_1_out), .out(shifter_1_out));
  Comparator #(.mode("unsigned"), .width(4)) comparator_5 (.a(op), .b(4'b0111), .eq(comparator_5_eq));  // open: gt, lt
  FPAdder #(.fpwidth(64)) fpadder_1 (.a(argY), .b(argZ), .out(fpadder_1_out));
  Comparator #(.mode("unsigned"), .width(4)) comparator_6 (.a(op), .b(4'b1000), .eq(comparator_6_eq));  // open: gt, lt
  // FPTrigonometry #(.fpwidth(64)) fptrigonometry_1: pin names not known; wires that end beside it: argX, argY, argZ, fptrigonometry_1_p4, fptrigonometry_1_p5, fptrigonometry_1_p6
  Comparator #(.mode("unsigned"), .width(4)) comparator_7 (.a(op), .b(4'b1001), .eq(comparator_7_eq));  // open: gt, lt
  BitFinder #(.width(64)) bitfinder_1 (.in(argY), .index(bitfinder_1_index), .found(bitfinder_1_found));
  Multiplexer #(.select(2)) multiplexer_1 (
    .in0(comparator_2_eq), .in1(comparator_2_lt), .in2(fpcomparator_1_p6), .in3(fpcomparator_1_p7),
    .out(multiplexer_1_out), .sel(bitselector_2_out));
  Multiplexer #(.select(4), .width(64)) multiplexer_2 (
    .in0(adder_1_out), .in1(bit_extender_1_out), .in2(subtractor_1_out), .in3(bit_extender_3_out),
    .in4(multiplier_1_out), .in5(multiplier_1_cout), .in6(divider_1_out), .in7(divider_1_rem),
    .in8(negator_1_out), .in9(counter_1_q), .in10(undriven), .in11(multiplexer_13_out),
    .in12(multiplexer_14_out), .out(multiplexer_2_out), .sel(\var ));  // open: in13, in14, in15
  Subtractor #(.width(64)) subtractor_1 (
    .a(argY), .b(argZ), .out(subtractor_1_out), .bout(subtractor_1_bout));  // open: bin
  Multiplexer #(.select(4), .width(64)) multiplexer_3 (
    .in0(shifter_1_out), .in1(shifter_2_out), .in2(shifter_3_out), .in3(shifter_4_out), .in4(shifter_5_out),
    .in5(buffer_1_out), .in6(not_1_out), .in7(or_1_out), .in8(and_1_out), .in9(nand_1_out), .in10(nor_1_out),
    .in11(xor_1_out), .in12(xnor_1_out), .in13(multiplexer_11_out), .out(multiplexer_3_out), .sel(\var ));  // open: in14, in15
  Shifter #(.shift("lr"), .width(64)) shifter_2 (.in(argY), .\dist (bitselector_1_out), .out(shifter_2_out));
  Multiplexer #(.select(4), .width(64)) multiplexer_4 (
    .in0(fpadder_1_out), .in1(fpsubtractor_1_out), .in2(fpmultiplier_1_out), .in3(fpdivider_1_out),
    .in4(fpnegator_1_p2), .in5(inttofp_1_p1), .in6(fptoint_1_p1), .in7(fptoint_2_p1), .in8(fptoint_3_p1),
    .in9(fptoint_4_p1), .in10(bit_extender_7_out), .in11(bit_extender_8_out), .out(multiplexer_4_out),
    .sel(\var ));  // open: in12, in13, in14, in15
  FPSubtractor #(.fpwidth(64)) fpsubtractor_1 (.a(argY), .b(argZ), .out(fpsubtractor_1_out));
  Multiplexer #(.select(4), .width(64)) multiplexer_5 (
    .in0(fptrigonometry_1_p4), .in1(fptrigonometry_1_p5), .in2(fptrigonometry_1_p6),
    .in3(fptrigonometry_2_p2), .in4(fptrigonometry_2_p3), .in5(fptrigonometry_2_p4), .in6(fplogarithm_1_p3),
    .in7(fpexponentiator_1_p1), .in8(fpsquareroot_1_p1), .out(multiplexer_5_out), .sel(\var ));  // open: in9, in10, in11, in12, in13, in14, in15
  // FPTrigonometry #(.fpwidth(64), .\type ("arc")) fptrigonometry_2: pin names not known; wires that end beside it: argY, fptrigonometry_2_p2, fptrigonometry_2_p3, fptrigonometry_2_p4
  Multiplexer #(.select(4), .width(64)) multiplexer_6 (
    .in0(multiplexer_7_out), .in1(multiplexer_8_out), .in2(multiplexer_10_out), .in3(multiplexer_12_out),
    .in4(bit_extender_9_out), .out(multiplexer_6_out), .sel(\var ));  // open: in5, in6, in7, in8, in9, in10, in11, in12, in13, in14, in15
  assign bit_extender_2_out = {{58{1'b0}}, bitfinder_1_index};  // Bit_Extender bit_extender_2
  Multiplexer #(.width(64)) multiplexer_7 (
    .in0(bit_extender_2_out), .in1({64{1'b1}}), .out(multiplexer_7_out), .sel(bitfinder_1_found));
  assign bit_extender_3_out = {{63{1'b0}}, subtractor_1_bout};  // Bit_Extender bit_extender_3
  Shifter #(.shift("ar"), .width(64)) shifter_3 (.in(argY), .\dist (bitselector_1_out), .out(shifter_3_out));
  FPMultiplier #(.fpwidth(64)) fpmultiplier_1 (.a(argY), .b(argZ), .out(fpmultiplier_1_out));
  // FPLogarithm #(.fpwidth(64)) fplogarithm_1: pin names not known; wires that end beside it: argY, argZ, fplogarithm_1_p3, argY, argZ
  BitFinder #(.\type ("high1"), .width(64)) bitfinder_2 (
    .in(argY), .index(bitfinder_2_index), .found(bitfinder_2_found));
  Multiplier #(.width(64)) multiplier_1 (
    .a(argY), .b(argZ), .out(multiplier_1_out), .cout(multiplier_1_cout));  // open: cin
  Shifter #(.shift("rl"), .width(64)) shifter_4 (.in(argY), .\dist (bitselector_1_out), .out(shifter_4_out));
  FPDivider #(.fpwidth(64)) fpdivider_1 (.a(argY), .b(argZ), .out(fpdivider_1_out));
  // FPExponentiator #(.fpwidth(64)) fpexponentiator_1: pin names not known; wires that end beside it: fpexponentiator_1_p1, argY
  assign bit_extender_4_out = {{58{1'b0}}, bitfinder_2_index};  // Bit_Extender bit_extender_4
  Multiplexer #(.width(64)) multiplexer_8 (
    .in0(bit_extender_4_out), .in1({64{1'b1}}), .out(multiplexer_8_out), .sel(bitfinder_2_found));
  Multiplexer #(.width(64)) multiplexer_9 (
    .in0({64{1'b0}}), .in1(64'h1), .out(multiplexer_9_out), .sel(multiplexer_1_out));
  Divider #(.mode("twosComplement"), .width(64)) divider_1 (
    .a(argY), .b(argZ), .out(divider_1_out), .rem(divider_1_rem));  // open: upper
  assign not_1_out = ~argY;  // NOT_Gate not_1, 64 bits wide
  assign buffer_1_out = argY;  // Buffer buffer_1, 64 bits wide
  Shifter #(.shift("rr"), .width(64)) shifter_5 (.in(argY), .\dist (bitselector_1_out), .out(shifter_5_out));
  // FPNegator #(.fpwidth(64)) fpnegator_1: pin names not known; wires that end beside it: argY, fpnegator_1_p2, argY
  // IntToFP #(.fpwidth(64), .width(64)) inttofp_1: pin names not known; wires that end beside it: inttofp_1_p1, argY
  // FPSquareRoot #(.fpwidth(64)) fpsquareroot_1: pin names not known; wires that end beside it: fpsquareroot_1_p1
  Negator #(.width(64)) negator_1 (.in(argY), .out(negator_1_out));
  assign nand_1_out = ~(argY & argZ);  // NAND_Gate nand_1, 64 bits wide
  assign or_1_out = argY | argZ;  // OR_Gate or_1, 64 bits wide
  assign and_1_out = argY & argZ;  // AND_Gate and_1, 64 bits wide
  // FPToInt #(.fpwidth(64), .width(64)) fptoint_1: pin names not known; wires that end beside it: fptoint_1_p1, argY
  assign bit_extender_5_out = {{58{1'b0}}, bitfinder_3_index};  // Bit_Extender bit_extender_5
  BitFinder #(.\type ("low0"), .width(64)) bitfinder_3 (
    .in(argY), .index(bitfinder_3_index), .found(bitfinder_3_found));
  Comparator #(.mode("unsigned"), .width(4)) comparator_8 (
    .a(\var ), .b(4'b1001), .eq(comparator_8_eq));  // open: gt, lt
  and and_2 (and_2_out, comparator_8_eq, comparator_3_eq);
  not not_2 (not_2_out, comparator_9_eq);
  Comparator #(.width(64)) comparator_9 (.a({64{1'b0}}), .b(argZ), .eq(comparator_9_eq));  // open: gt, lt
  assign nor_1_out = ~(argY | argZ);  // NOR_Gate nor_1, 64 bits wide
  assign xor_1_out = argY ^ argZ;  // XOR_Gate xor_1, 64 bits wide
  // FPToInt #(.fpwidth(64), .mode("floor"), .width(64)) fptoint_2: pin names not known; wires that end beside it: fptoint_2_p1, argY
  Multiplexer #(.width(64)) multiplexer_10 (
    .in0(bit_extender_5_out), .in1({64{1'b1}}), .out(multiplexer_10_out), .sel(bitfinder_3_found));
  and and_3 (and_3_out, and_2_out, not_2_out);
  Counter #(.max('hffffffffffffffff), .width(64)) counter_1 (
    .load(and_3_out), .D(argY), .Q(counter_1_q), .clk(clock_1_out));  // open: count, carry, up, clr
  Clock clock_1 (.out(clock_1_out));
  assign xnor_1_out = ~(argY ^ argZ);  // XNOR_Gate xnor_1, 64 bits wide
  // FPToInt #(.fpwidth(64), .mode("ceil"), .width(64)) fptoint_3: pin names not known; wires that end beside it: fptoint_3_p1, argY
  BitFinder #(.\type ("high0"), .width(64)) bitfinder_4 (
    .in(argY), .index(bitfinder_4_index), .found(bitfinder_4_found));
  Random #(.seed(12345667), .width(64)) random_1 ();  // open: clk, next, out, clr
  Clock clock_2 (.out(clock_2_out));
  Multiplexer #(.width(64)) multiplexer_11 (.in0(argX), .in1(buffer_2_out), .out(multiplexer_11_out), .sel(not_3_out));
  assign buffer_2_out = argY;  // Buffer buffer_2, 64 bits wide
  not not_3 (not_3_out, comparator_10_eq);
  Comparator #(.mode("unsigned"), .width(64)) comparator_10 (
    .a(argZ), .b({64{1'b0}}), .eq(comparator_10_eq));  // open: gt, lt
  // FPToInt #(.fpwidth(64), .mode("truncate"), .width(64)) fptoint_4: pin names not known; wires that end beside it: fptoint_4_p1, argY
  assign bit_extender_6_out = {{58{1'b0}}, bitfinder_4_index};  // Bit_Extender bit_extender_6
  Multiplexer #(.width(64)) multiplexer_12 (
    .in0(bit_extender_6_out), .in1({64{1'b1}}), .out(multiplexer_12_out), .sel(bitfinder_4_found));
  // FPClassificator #(.fpwidth(64)) fpclassificator_1: pin names not known; wires that end beside it: fpclassificator_1_p1, fpclassificator_1_p2
  BitAdder #(.width(64)) bitadder_1 (.in0(argY), .out(bitadder_1_out));
  Comparator #(.mode("unsigned"), .width(4)) comparator_11 (
    .a(\var ), .b(4'b1100), .eq(comparator_11_eq));  // open: gt, lt
  and and_4 (and_4_out, comparator_11_eq, comparator_3_eq);
  not not_4 (not_4_out, comparator_12_eq);
  Comparator #(.width(64)) comparator_12 (.a({64{1'b0}}), .b(argZ), .eq(comparator_12_eq));  // open: gt, lt
  assign bit_extender_7_out = {{63{1'b0}}, fpclassificator_1_p1};  // Bit_Extender bit_extender_7
  assign bit_extender_8_out = {{63{1'b0}}, fpclassificator_1_p2};  // Bit_Extender bit_extender_8
  assign bit_extender_9_out = {{57{1'b0}}, bitadder_1_out};  // Bit_Extender bit_extender_9
  Comparator #(.width(64)) comparator_13 (.a({64{1'b0}}), .b(register_1_q), .eq(comparator_13_eq));  // open: gt, lt
  Register #(.width(64)) register_1 (.D(argY), .en(and_5_out), .clk(clock_3_out), .Q(register_1_q));  // open: clr
  and and_5 (and_5_out, and_4_out, not_4_out);
  Clock clock_3 (.out(clock_3_out));
  Multiplexer #(.width(64)) multiplexer_13 (
    .in0(register_1_q), .in1(64'h5f5e100), .out(multiplexer_13_out), .sel(comparator_13_eq));
  BitSelector #(.width(64)) bitselector_3 (.in(argY), .out(bitselector_3_out), .sel({6{1'b0}}));
  Multiplexer #(.width(64)) multiplexer_14 (
    .in0({64{1'b0}}), .in1(64'h1), .out(multiplexer_14_out), .sel(bitselector_3_out));
  or or_2 (we, comparator_1_eq, comparator_3_eq, comparator_4_eq, comparator_5_eq, comparator_6_eq, comparator_7_eq);
  Multiplexer #(.select(4), .width(64)) multiplexer_15 (
    .in4(multiplexer_9_out), .in5(multiplexer_2_out), .in6(multiplexer_3_out), .in7(multiplexer_4_out),
    .in8(multiplexer_5_out), .in9(multiplexer_6_out), .out(outX), .sel(op));  // open: in0, in1, in2, in3, in10, in11, in12, in13, in14, in15
endmodule

module core256 (
);

  wire and_1_out, and_2_out, and_4_out, bitselector_9_out, bitselector_10_out, clock_1_out, clock_2_out,
       clock_3_out, clock_6_out, clock_9_out, clock_12_out, comparator_1_eq, comparator_2_eq,
       comparator_3_eq, comparator_4_eq, comparator_5_eq, comparator_5_gt, comparator_5_lt, comparator_6_eq,
       LE0, LE1, LE2, LE3, LE4, LE5, LE6, LE7, LE8, LE9, LE10, LE11, LE12, LE13, LE14, LE15, LE16, LE17,
       LE18, LE19, LE20, LE21, LE22, LE23, LE24, LE25, LE26, LE27, LE28, LE29, LE30, LE31, multiplexer_1_out,
       not_1_out, not_2_out, not_3_out, not_4_out, or_1_out, regY1_p28, regY2_p36, regY3_p36, regY4_p36,
       regZ1_p11, regZ2_p19, regZ3_p19, regZ4_p19, WE;
  wire [3:0] INSO, INSV;
  wire [15:0] bitselector_7_out, bitselector_8_out;
  wire [23:0] bitselector_11_out, prog1_q, REGX, REGY, REGZ;
  wire [63:0] nop1_q, regX2_p1, regX3_p1, regX4_p1, regX4_p5, X1I0, X1I1, X1I2, X1I3, X1I4, X1I5, X1I6, X1I7,
       X1O8, X1O9, X1O10, X1O11, X1O12, X1O13, X1O14, X1O15, X2I0, X2I1, X2I2, X2I3, X2I4, X2I5, X2I6, X2I7,
       X2O8, X2O9, X2O10, X2O11, X2O12, X2O13, X2O14, X2O15, X3I0, X3I1, X3I2, X3I3, X3I4, X3I5, X3I6, X3I7,
       X3O8, X3O9, X3O10, X3O11, X3O12, X3O13, X3O14, X3O15, X4I0, X4I1, X4I2, X4I3, X4I4, X4I5, X4I6, X4I7,
       X4O8, X4O9, X4O10, X4O11, X4O12, X4O13, X4O14, X4O15, Y1O8, Y1O9, Y1O10, Y1O11, Y1O12, Y1O13, Y1O14,
       Y1O15, Y2O8, Y2O9, Y2O10, Y2O11, Y2O12, Y2O13, Y2O14, Y2O15, Y3O8, Y3O9, Y3O10, Y3O11, Y3O12, Y3O13,
       Y3O14, Y3O15, Y4O8, Y4O9, Y4O10, Y4O11, Y4O12, Y4O13, Y4O14, Y4O15;

  BitSelector #(.group(24), .width(64)) bitselector_1 (.in(regX4_p5), .out(REGX), .sel(2'b00));
  BitSelector #(.group(24), .width(64)) bitselector_2 (.in(regX4_p1), .out(REGY), .sel(2'b00));
  BitSelector #(.group(4), .width(16)) bitselector_3 (.in(bitselector_7_out), .out(INSV), .sel(2'b00));
  BitSelector #(.group(4), .width(16)) bitselector_4 (.in(bitselector_8_out), .out(INSO), .sel(2'b00));
  BitSelector #(.group(24), .width(64)) bitselector_5 (.in(regX3_p1), .out(REGZ), .sel(2'b00));
  // Probe on regX4_p5
  // Probe on regX4_p1
  // Probe on regX3_p1
  // Probe on regX2_p1
  // Probe on {LE31, LE30, LE29, LE28, LE27, LE26, LE25, LE24, LE23, LE22, LE21, LE20, LE19, LE18, LE17, LE16, LE15, LE14, LE13, LE12, LE11, LE10, LE9, LE8, LE7, LE6, LE5, LE4, LE3, LE2, LE1, LE0}
  // Probe on bitselector_7_out
  // Probe on bitselector_8_out
  BitSelector #(.group(32), .width(64)) bitselector_6 (
    .in(regX2_p1),
    .out({LE31, LE30, LE29, LE28, LE27, LE26, LE25, LE24, LE23, LE22, LE21, LE20, LE19, LE18, LE17, LE16, LE15, LE14, LE13, LE12, LE11, LE10, LE9, LE8, LE7, LE6, LE5, LE4, LE3, LE2, LE1, LE0}),
    .sel(1'b1));
  BitSelector #(.group(16), .width(64)) bitselector_7 (.in(regX2_p1), .out(bitselector_7_out), .sel(2'b01));
  BitSelector #(.group(16), .width(64)) bitselector_8 (.in(regX2_p1), .out(bitselector_8_out), .sel(2'b00));
  Comparator #(.mode("unsigned"), .width(16)) comparator_1 (
    .a(bitselector_8_out), .b({16{1'b0}}), .eq(comparator_1_eq));  // open: gt, lt
  Clock clock_1 (.out(clock_1_out));
  Comparator #(.mode("unsigned"), .width(16)) comparator_2 (
    .a(bitselector_8_out), .b(16'h1), .eq(comparator_2_eq));  // open: gt, lt
  not not_1 (not_1_out, bitselector_9_out);
  BitSelector #(.width(16)) bitselector_9 (.in(bitselector_7_out), .out(bitselector_9_out), .sel(4'b0000));
  Comparator #(.mode("unsigned"), .width(16)) comparator_3 (
    .a(bitselector_8_out), .b(16'h2), .eq(comparator_3_eq));  // open: gt, lt
  Comparator #(.mode("unsigned"), .width(16)) comparator_4 (
    .a(bitselector_8_out), .b(16'h3), .eq(comparator_4_eq));  // open: gt, lt
  BitSelector #(.width(16)) bitselector_10 (.in(bitselector_7_out), .out(bitselector_10_out), .sel(4'b0000));
  Counter #(.max('hffffffffffffffff), .width(64)) nop1 (
    .load(or_1_out), .D({64{1'b0}}), .count(comparator_1_eq), .Q(nop1_q), .clk(clock_1_out));  // open: carry, up, clr
  Comparator #(.mode("unsigned"), .width(64)) comparator_5 (
    .a(nop1_q), .b(regX3_p1), .gt(comparator_5_gt), .eq(comparator_5_eq), .lt(comparator_5_lt));
  not not_2 (not_2_out, bitselector_10_out);
  or or_1 (or_1_out, comparator_5_gt, comparator_5_eq);
  and and_1 (and_1_out, comparator_5_lt, comparator_1_eq);
  not not_3 (not_3_out, comparator_6_eq);
  Comparator #(.mode("unsigned"), .width(64)) comparator_6 (
    .a(Y1O8), .b({64{1'b0}}), .eq(comparator_6_eq));  // open: gt, lt
  and and_2 (and_2_out, comparator_4_eq, not_2_out);
  // AND_Gate and_3 has open pins: in0=comparator_4_eq, in1=bitselector_10_out, out=open
  and and_4 (and_4_out, not_3_out, comparator_2_eq);
  Multiplexer multiplexer_1 (.in0(and_4_out), .in1(comparator_2_eq), .out(multiplexer_1_out), .sel(not_1_out));
  or or_2 (WE, comparator_3_eq, and_2_out);
  not not_4 (not_4_out, and_1_out);
  BitSelector #(.group(24), .width(64)) bitselector_11 (.in(X1O8), .out(bitselector_11_out), .sel(2'b00));
  Counter #(.max('hffffff), .trigger("falling"), .width(24)) prog1 (
    .load(multiplexer_1_out), .D(bitselector_11_out), .count(not_4_out), .Q(prog1_q), .clk(clock_2_out));  // open: carry, up, clr
  Clock clock_2 (.out(clock_2_out));
  Multiplexer #(.select(4), .width(64)) multiplexer_2 (
    .in2(regX3_p1), .out(X1I0), .sel(INSO));  // open: in0, in1, in3, in4, in5, in6, in7, in8, in9, in10, in11, in12, in13, in14, in15
  Multiplexer #(.select(4), .width(64)) multiplexer_3 (
    .in2(regX3_p1), .out(X1I1), .sel(INSO));  // open: in0, in1, in3, in4, in5, in6, in7, in8, in9, in10, in11, in12, in13, in14, in15
  Multiplexer #(.select(4), .width(64)) multiplexer_4 (
    .in2(regX3_p1), .out(X1I2), .sel(INSO));  // open: in0, in1, in3, in4, in5, in6, in7, in8, in9, in10, in11, in12, in13, in14, in15
  Multiplexer #(.select(4), .width(64)) multiplexer_5 (
    .in2(regX3_p1), .out(X1I3), .sel(INSO));  // open: in0, in1, in3, in4, in5, in6, in7, in8, in9, in10, in11, in12, in13, in14, in15
  Multiplexer #(.select(4), .width(64)) multiplexer_6 (
    .in2(regX3_p1), .out(X1I4), .sel(INSO));  // open: in0, in1, in3, in4, in5, in6, in7, in8, in9, in10, in11, in12, in13, in14, in15
  Multiplexer #(.select(4), .width(64)) multiplexer_7 (
    .in2(regX3_p1), .out(X1I5), .sel(INSO));  // open: in0, in1, in3, in4, in5, in6, in7, in8, in9, in10, in11, in12, in13, in14, in15
  Multiplexer #(.select(4), .width(64)) multiplexer_8 (
    .in2(regX3_p1), .out(X1I6), .sel(INSO));  // open: in0, in1, in3, in4, in5, in6, in7, in8, in9, in10, in11, in12, in13, in14, in15
  Multiplexer #(.select(4), .width(64)) multiplexer_9 (
    .in2(regX3_p1), .out(X1I7), .sel(INSO));  // open: in0, in1, in3, in4, in5, in6, in7, in8, in9, in10, in11, in12, in13, in14, in15
  Multiplexer #(.select(4), .width(64)) multiplexer_10 (
    .in2(regX3_p1), .out(X2I0), .sel(INSO));  // open: in0, in1, in3, in4, in5, in6, in7, in8, in9, in10, in11, in12, in13, in14, in15
  Multiplexer #(.select(4), .width(64)) multiplexer_11 (
    .in2(regX3_p1), .out(X2I1), .sel(INSO));  // open: in0, in1, in3, in4, in5, in6, in7, in8, in9, in10, in11, in12, in13, in14, in15
  Multiplexer #(.select(4), .width(64)) multiplexer_12 (
    .in2(regX3_p1), .out(X2I2), .sel(INSO));  // open: in0, in1, in3, in4, in5, in6, in7, in8, in9, in10, in11, in12, in13, in14, in15
  Multiplexer #(.select(4), .width(64)) multiplexer_13 (
    .in2(regX3_p1), .out(X2I3), .sel(INSO));  // open: in0, in1, in3, in4, in5, in6, in7, in8, in9, in10, in11, in12, in13, in14, in15
  Multiplexer #(.select(4), .width(64)) multiplexer_14 (
    .in2(regX3_p1), .out(X2I4), .sel(INSO));  // open: in0, in1, in3, in4, in5, in6, in7, in8, in9, in10, in11, in12, in13, in14, in15
  Multiplexer #(.select(4), .width(64)) multiplexer_15 (
    .in2(regX3_p1), .out(X2I5), .sel(INSO));  // open: in0, in1, in3, in4, in5, in6, in7, in8, in9, in10, in11, in12, in13, in14, in15
  Multiplexer #(.select(4), .width(64)) multiplexer_16 (
    .in2(regX3_p1), .out(X2I6), .sel(INSO));  // open: in0, in1, in3, in4, in5, in6, in7, in8, in9, in10, in11, in12, in13, in14, in15
  Multiplexer #(.select(4), .width(64)) multiplexer_17 (
    .in2(regX3_p1), .out(X2I7), .sel(INSO));  // open: in0, in1, in3, in4, in5, in6, in7, in8, in9, in10, in11, in12, in13, in14, in15
  Multiplexer #(.select(4), .width(64)) multiplexer_18 (
    .in2(regX3_p1), .out(X3I0), .sel(INSO));  // open: in0, in1, in3, in4, in5, in6, in7, in8, in9, in10, in11, in12, in13, in14, in15
  Multiplexer #(.select(4), .width(64)) multiplexer_19 (
    .in2(regX3_p1), .out(X3I1), .sel(INSO));  // open: in0, in1, in3, in4, in5, in6, in7, in8, in9, in10, in11, in12, in13, in14, in15
  Multiplexer #(.select(4), .width(64)) multiplexer_20 (
    .in2(regX3_p1), .out(X3I2), .sel(INSO));  // open: in0, in1, in3, in4, in5, in6, in7, in8, in9, in10, in11, in12, in13, in14, in15
  Multiplexer #(.select(4), .width(64)) multiplexer_21 (
    .in2(regX3_p1), .out(X3I3), .sel(INSO));  // open: in0, in1, in3, in4, in5, in6, in7, in8, in9, in10, in11, in12, in13, in14, in15
  Multiplexer #(.select(4), .width(64)) multiplexer_22 (
    .in2(regX3_p1), .out(X3I4), .sel(INSO));  // open: in0, in1, in3, in4, in5, in6, in7, in8, in9, in10, in11, in12, in13, in14, in15
  Multiplexer #(.select(4), .width(64)) multiplexer_23 (
    .in2(regX3_p1), .out(X3I5), .sel(INSO));  // open: in0, in1, in3, in4, in5, in6, in7, in8, in9, in10, in11, in12, in13, in14, in15
  Multiplexer #(.select(4), .width(64)) multiplexer_24 (
    .in2(regX3_p1), .out(X3I6), .sel(INSO));  // open: in0, in1, in3, in4, in5, in6, in7, in8, in9, in10, in11, in12, in13, in14, in15
  Multiplexer #(.select(4), .width(64)) multiplexer_25 (
    .in2(regX3_p1), .out(X3I7), .sel(INSO));  // open: in0, in1, in3, in4, in5, in6, in7, in8, in9, in10, in11, in12, in13, in14, in15
  Multiplexer #(.select(4), .width(64)) multiplexer_26 (
    .in2(regX3_p1), .out(X4I0), .sel(INSO));  // open: in0, in1, in3, in4, in5, in6, in7, in8, in9, in10, in11, in12, in13, in14, in15
  Multiplexer #(.select(4), .width(64)) multiplexer_27 (
    .in2(regX3_p1), .out(X4I1), .sel(INSO));  // open: in0, in1, in3, in4, in5, in6, in7, in8, in9, in10, in11, in12, in13, in14, in15
  Multiplexer #(.select(4), .width(64)) multiplexer_28 (
    .in2(regX3_p1), .out(X4I2), .sel(INSO));  // open: in0, in1, in3, in4, in5, in6, in7, in8, in9, in10, in11, in12, in13, in14, in15
  Multiplexer #(.select(4), .width(64)) multiplexer_29 (
    .in2(regX3_p1), .out(X4I3), .sel(INSO));  // open: in0, in1, in3, in4, in5, in6, in7, in8, in9, in10, in11, in12, in13, in14, in15
  Multiplexer #(.select(4), .width(64)) multiplexer_30 (
    .in2(regX3_p1), .out(X4I4), .sel(INSO));  // open: in0, in1, in3, in4, in5, in6, in7, in8, in9, in10, in11, in12, in13, in14, in15
  Multiplexer #(.select(4), .width(64)) multiplexer_31 (
    .in2(regX3_p1), .out(X4I5), .sel(INSO));  // open: in0, in1, in3, in4, in5, in6, in7, in8, in9, in10, in11, in12, in13, in14, in15
  Multiplexer #(.select(4), .width(64)) multiplexer_32 (
    .in2(regX3_p1), .out(X4I6), .sel(INSO));  // open: in0, in1, in3, in4, in5, in6, in7, in8, in9, in10, in11, in12, in13, in14, in15
  Multiplexer #(.select(4), .width(64)) multiplexer_33 (
    .in2(regX3_p1), .out(X4I7), .sel(INSO));  // open: in0, in1, in3, in4, in5, in6, in7, in8, in9, in10, in11, in12, in13, in14, in15
  // DualRAM #(.addrWidth(24), .dataWidth(64), .enables("line"), .line("octo"), .misaligned("true")) regX1: pin names not known; wires that end beside it: prog1_q, REGX, WE
  Clock clock_3 (.out(clock_3_out));
  // DualRAM #(.addrWidth(24), .dataWidth(64), .enables("line"), .line("octo"), .misaligned("true")) regY1: pin names not known; wires that end beside it: WE, LE1, LE2, LE3, LE4, LE5, LE6, LE7, clock_3_out, X1I0, X1I1, X1I2, X1I3, X1I4, X1I5, X1I6, X1I7, REGX, WE, WE, LE1, LE2, LE3, LE4, LE5, LE6, LE7, regY1_p28, X1I0, X1I1, X1I2, X1I3, X1I4, X1I5, X1I6, X1I7, REGY
  Clock clock_4 (.out(regY1_p28));
  // DualRAM #(.addrWidth(24), .dataWidth(64), .enables("line"), .line("octo"), .misaligned("true")) regZ1: pin names not known; wires that end beside it: REGX, WE, WE, LE1, LE2, LE3, LE4, LE5, LE6, LE7, regZ1_p11, X1I0, X1I1, X1I2, X1I3, X1I4, X1I5, X1I6, X1I7, REGZ
  Clock clock_5 (.out(regZ1_p11));
  // DualRAM #(.addrWidth(24), .dataWidth(64), .enables("line"), .line("octo"), .misaligned("true")) regX2: pin names not known; wires that end beside it: regX2_p1, prog1_q, REGX, WE
  Clock clock_6 (.out(clock_6_out));
  // DualRAM #(.addrWidth(24), .dataWidth(64), .enables("line"), .line("octo"), .misaligned("true")) regY2: pin names not known; wires that end beside it: X1O8, X1O9, X1O10, X1O11, X1O12, X1O13, X1O14, X1O15, WE, LE9, LE10, LE11, LE12, LE13, LE14, LE15, clock_6_out, X2I0, X2I1, X2I2, X2I3, X2I4, X2I5, X2I6, X2I7, REGX, WE, WE, LE9, LE10, LE11, LE12, LE13, LE14, LE15, regY2_p36, X2I0, X2I1, X2I2, X2I3, X2I4, X2I5, X2I6, X2I7, REGY
  Clock clock_7 (.out(regY2_p36));
  // DualRAM #(.addrWidth(24), .dataWidth(64), .enables("line"), .line("octo"), .misaligned("true")) regZ2: pin names not known; wires that end beside it: Y1O8, Y1O9, Y1O10, Y1O11, Y1O12, Y1O13, Y1O14, Y1O15, REGX, WE, WE, LE9, LE10, LE11, LE12, LE13, LE14, LE15, regZ2_p19, X2I0, X2I1, X2I2, X2I3, X2I4, X2I5, X2I6, X2I7, REGZ
  Clock clock_8 (.out(regZ2_p19));
  // DualRAM #(.addrWidth(24), .dataWidth(64), .enables("line"), .line("octo"), .misaligned("true")) regX3: pin names not known; wires that end beside it: regX3_p1, prog1_q, REGX, WE
  Clock clock_9 (.out(clock_9_out));
  // DualRAM #(.addrWidth(24), .dataWidth(64), .enables("line"), .line("octo"), .misaligned("true")) regY3: pin names not known; wires that end beside it: X2O8, X2O9, X2O10, X2O11, X2O12, X2O13, X2O14, X2O15, WE, LE17, LE18, LE19, LE20, LE21, LE22, LE23, clock_9_out, X3I0, X3I1, X3I2, X3I3, X3I4, X3I5, X3I6, X3I7, REGX, WE, WE, LE17, LE18, LE19, LE20, LE21, LE22, LE23, regY3_p36, X3I0, X3I1, X3I2, X3I3, X3I4, X3I5, X3I6, X3I7, REGY
  Clock clock_10 (.out(regY3_p36));
  // DualRAM #(.addrWidth(24), .dataWidth(64), .enables("line"), .line("octo"), .misaligned("true")) regZ3: pin names not known; wires that end beside it: Y2O8, Y2O9, Y2O10, Y2O11, Y2O12, Y2O13, Y2O14, Y2O15, REGX, WE, WE, LE17, LE18, LE19, LE20, LE21, LE22, LE23, regZ3_p19, X3I0, X3I1, X3I2, X3I3, X3I4, X3I5, X3I6, X3I7, REGZ
  Clock clock_11 (.out(regZ3_p19));
  // DualRAM #(.addrWidth(24), .dataWidth(64), .enables("line"), .line("octo"), .misaligned("true")) regX4: pin names not known; wires that end beside it: regX4_p1, prog1_q, REGX, WE, regX4_p5
  Clock clock_12 (.out(clock_12_out));
  // DualRAM #(.addrWidth(24), .dataWidth(64), .enables("line"), .line("octo"), .misaligned("true")) regY4: pin names not known; wires that end beside it: X3O8, X3O9, X3O10, X3O11, X3O12, X3O13, X3O14, X3O15, WE, LE25, LE26, LE27, LE28, LE29, LE30, LE31, clock_12_out, X4I0, X4I1, X4I2, X4I3, X4I4, X4I5, X4I6, X4I7, REGX, WE, WE, LE25, LE26, LE27, LE28, LE29, LE30, LE31, regY4_p36, X4I0, X4I1, X4I2, X4I3, X4I4, X4I5, X4I6, X4I7, REGY, X4O8, X4O9, X4O10, X4O11, X4O12, X4O13, X4O14, X4O15
  Clock clock_13 (.out(regY4_p36));
  // DualRAM #(.addrWidth(24), .dataWidth(64), .enables("line"), .line("octo"), .misaligned("true")) regZ4: pin names not known; wires that end beside it: Y3O8, Y3O9, Y3O10, Y3O11, Y3O12, Y3O13, Y3O14, Y3O15, REGX, WE, WE, LE25, LE26, LE27, LE28, LE29, LE30, LE31, regZ4_p19, X4I0, X4I1, X4I2, X4I3, X4I4, X4I5, X4I6, X4I7, REGZ, Y4O8, Y4O9, Y4O10, Y4O11, Y4O12, Y4O13, Y4O14, Y4O15
  Clock clock_14 (.out(regZ4_p19));

  // Other names for the same wires on the sheet: VECN[31:0] = {LE31, LE30, LE29, LE28, LE27, LE26, LE25, LE24, LE23, LE22, LE21, LE20, LE19, LE18, LE17, LE16, LE15, LE14, LE13, LE12, LE11, LE10, LE9, LE8, LE7, LE6, LE5, LE4, LE3, LE2, LE1, LE0}
endmodule
